# Fritzing sketch HamradioSequencer (saved by Fritzing 0.9.3b)

parts:
  U1 = 4-Channel 5v Relay Shield [package=relay-4ch5v10a]
  Part1 = Arduino Nano (Rev3.0)  # not connected
  S1 = Round Pushbutton

nets:
  N1: U1.GND, S1.leg1
  N2: U1.IN3, S1.leg0

custom parts:
  4-Channel 5v Relay Shield: 4 Channel 5v Relay Shield w. 2x SPD-06VDC-SD-C
